# Fritzing sketch Humidifier (saved by Fritzing 0.9.3b)
circuit board: 5.47689cm x 3.86459cm
breadboards: 1

parts:
  ESP32 = Heltec WiFi Kit [part_number=HTIT-WB32]
  BMP180 = Barometric Pressure Sensor - BMP180 Breakout (GY-68)
  ONOFF = Pushbutton [package="[THT]"]
  RST = Pushbutton [package="[THT]"]
  R1 = Resistor [tolerance=±5% power=0.25 resistance=1k package=THT]
  Q1 = NPN-Transistor [part_number=S8050 package="TO92 [THT]"]
  BZR = Buzzer
  R2 = Resistor [tolerance=±5% power=0.25 resistance=100 package=THT]
  J2 = male pin header, 6 pins [form="♂ (male)"]

nets:
  N1: ESP32.pin_2, BMP180.SCL
  N2: ESP32.pin_6, BZR.pin2
  N3: ESP32.pin_7, ONOFF.Pin_3, ONOFF.Pin_4
  N4: ESP32.pin_9, RST.Pin_3, RST.Pin_4
  N5: ESP32.pin_16, ESP32.pin_17, J2.pin4
  GND: ESP32.GND, BMP180.GND, ONOFF.Pin_1, ONOFF.Pin_2, RST.Pin_1, RST.Pin_2, Q1.E, BZR.pin1, R2.Pin_1, J2.pin6
  N6: ESP32.pin_20, BMP180.VCC, J2.pin5
  N7: ESP32.pin_21, ESP32.pin_22
  N8: ESP32.pin_25, BMP180.SDA
  N9: ESP32.pin_28, R1.Pin_0
  N10: ESP32.pin_31, R2.Pin_0, J2.pin1
  N11: R1.Pin_1, Q1.B
  N12: Q1.C, J2.pin2

notes:
  IG

custom parts:
  Heltec WiFi Kit: The Heltec WiFi Kit 32 is an IoT development board designed and produced by Heltec Automation and based on the Espressif ESP32. The board includes WiFi and Bluetooth functions, as well as a 0.96″ OLED display and a lithium battery management system.
  Buzzer: Fixed frequency buzzer
